// Logisim project Herasymuk_lab__ALU.circ as structural Verilog: 1 circuit, main circuit main
module main (
  input  A1,
  input  B1,
  input  A2,
  input  B2,
  input  Operation_code
);

  wire and_1_out, and_2_out, and_3_out, and_4_out, and_5_out, and_6_out, and_7_out, and_8_out, and_9_out,
       and_10_out, not_1_out, not_2_out, not_3_out, not_4_out, not_5_out, or_1_out, or_2_out, or_3_out,
       xnor_1_out, xor_1_out, xor_2_out, xor_3_out;

  xor xor_1 (xor_1_out, A1, B1);
  not not_1 (not_1_out, A1);
  and and_1 (and_1_out, A1, B1);
  not not_2 (not_2_out, A2);
  xnor xnor_1 (xnor_1_out, A2, B2);
  and and_2 (and_2_out, not_1_out, B1);
  xor xor_2 (xor_2_out, A2, B2);
  and and_3 (and_3_out, not_2_out, B2);
  and and_4 (and_4_out, xnor_1_out, and_2_out);
  xor xor_3 (xor_3_out, xor_2_out, and_1_out);
  and and_5 (and_5_out, xor_2_out, and_1_out);
  and and_6 (and_6_out, A2, B2);
  or or_1 (or_1_out, and_3_out, and_4_out);
  or or_2 (or_2_out, and_5_out, and_6_out);
  not not_3 (not_3_out, Operation_code);
  not not_4 (not_4_out, Operation_code);
  not not_5 (not_5_out, Operation_code);
  and and_7 (and_7_out, xor_1_out, not_3_out);
  and and_8 (and_8_out, xor_3_out, not_4_out);
  and and_9 (and_9_out, or_2_out, not_5_out);
  and and_10 (and_10_out, Operation_code, or_1_out);
  or or_3 (or_3_out, and_9_out, and_10_out);
  LED Sum1 (.in(and_7_out));
  LED Sum2 (.in(and_8_out));
  LED Carry_out (.in(or_3_out));

  // Notes on the sheet:
  //   Half_summator_for_first_bits
  //   ! A1 AND B1
  //   ! A2 AND B2
  //   Full_summator_for_second_bits
  //   (B2 XNOR A2) AND (! A1 AND B1)
endmodule
